# Fritzing sketch NodeMCU Obstacle Detector_layout (saved by Fritzing 0.9.3b)
circuit board: 8.46667cm x 5.64444cm
breadboards: 1

parts:
  U1 = NodeMCU V1.0
  J1 = Piezo Speaker
  hc-sr1 = hc-sr04
  LED1 = RGB LED - (4 legs) [package="5 mm [THT]"]

nets:
  N1: U1.D1, hc-sr1.Trig
  N2: U1.D2, hc-sr1.Echo
  3V3: U1.3V3, hc-sr1.VCC, LED1.common_anode
  GND: U1.GND, J1.pin1, hc-sr1.GND
  N3: U1.D5, LED1.red_cathode
  N4: U1.D6, LED1.green_cathode
  N5: U1.D7, LED1.blue_cathode

custom parts:
  NodeMCU V1.0: ESP8266 based NodeMCU
